# Fritzing sketch Vivero (saved by Fritzing 0.9.3b)
breadboards: 1

parts:
  M1 = DOIT Esp32 DevKit v1 (30 pins long, 11 pins width) [part_number=ESP32S-PIN30]
  Part1 = KY-015 Temperature & Humidity Sensor Module [package="Breakout board"]
  YL-83_-_Control_Board1 = YL-83 Rain Sensor - Control Board
  부품2 = FC-28 Soil Hygrometer Module - Probe

nets:
  3V3: M1.3V3, Part1.S, YL-83_-_Control_Board1.VCC
  GND: M1.GND, Part1.-, YL-83_-_Control_Board1.GND
  N1: M1.D15, Part1.Vin
  N2: M1.VN, YL-83_-_Control_Board1.AO
  N3: YL-83_-_Control_Board1.POS, 부품2.POS
  N4: YL-83_-_Control_Board1.NEG, 부품2.NEG

custom parts:
  DOIT Esp32 DevKit v1 (30 pins long, 11 pins width): The DOIT Esp32 DevKit v1 is one of the development board created by DOIT to evaluate the ESP-WROOM-32 module. It is based on the ESP32 microcontroller that boasts Wifi, Bluetooth, Ethernet and Low Power support all in a single chip. (vanepp) made breadboard work, adjusted pin numbering and labels and reduced size of schematic and cleaned up pcb. This chip is 30pins long (2 x15) and 11 pins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
  KY-015 Temperature & Humidity Sensor Module: KY-015 temperature and humidity sensor module, provides a low-latency serial interface to measure humidity and temperature.
  YL-83 Rain Sensor - Control Board: The YL-83 is a rain sensor that has more resistance when dry and less resistance when wet. The module runs at 5V.
  FC-28 Soil Hygrometer Module - Probe: The FC-28 is a soil hygrometer module that uses the Texas Instruments LM393 comparator chip to provide an analog measurement of soil humidity.
